# Fritzing sketch Driver motor de passo2 (saved by Fritzing 0.7.12b)
breadboards: 1

parts:
  Da = Rectifier Diode [part_number=1N4004 package="300 mil [THT]"]
  Db = Rectifier Diode [part_number=1N4004 package="300 mil [THT]"]
  Qd = npn-Powertransistor [part_number=TIP41C package="TO220 [THT]"]
  Qb = npn-Powertransistor [part_number=TIP41C package="TO220 [THT]"]
  Qc = npn-Powertransistor [part_number=TIP41C package="TO220 [THT]"]
  Rd = Resistor [tolerance=±5% resistance=220 package=THT]
  Rc = Resistor [tolerance=±5% resistance=220 package=THT]
  Dc = Rectifier Diode [part_number=1N4001 package="300 mil [THT]"]
  Power = Power plug
  GND = female pin header, 1 pin [form="♀ (female)"]
  Dd = Rectifier Diode [part_number=1N4004 package="300 mil [THT]"]
  Rb = Resistor [tolerance=±5% resistance=220 package=THT]
  Ra = Resistor [tolerance=±5% resistance=220 package=THT]
  Motor1 = screw terminal, 6 pins
  Qa = npn-Powertransistor [package="TO220 [THT]"]
  R1 = Resistor [tolerance=±5% resistance=220 package=THT]
  Q1 = npn-Powertransistor [package="TO220 [THT]"]
  Motor2 = screw terminal, 6 pins
  Motor3 = screw terminal, 6 pins
  J1 = female pin header, 7 pins [form="♀ (female)"]
  Q2 = npn-Powertransistor [package="TO220 [THT]"]
  R2 = Resistor [tolerance=±5% resistance=220 package=THT]
  Q3 = npn-Powertransistor [package="TO220 [THT]"]
  R3 = Resistor [tolerance=±5% resistance=220 package=THT]

nets (from the schematic view):
  N1: Da.cathode, Motor1.pin3, Qa.collector, Motor2.pin3, Motor3.pin3
  N2: Da.anode, Db.anode, Qd.emitter, Qb.emitter, Qc.emitter, Dc.anode, Power.GND, GND.pin1, Dd.anode, Qa.emitter
  N3: Db.cathode, Qb.collector, Motor1.pin4, Motor2.pin4, Motor3.pin4
  N4: Qd.base, Rd.Pin_0
  N5: Qd.collector, Dd.cathode, Motor1.pin6, Motor2.pin6, Motor3.pin6
  N6: Qb.base, Rb.Pin_0
  N7: Qc.base, Rc.Pin_0
  N8: Qc.collector, Dc.cathode, Motor1.pin5, Motor2.pin5, Motor3.pin5
  N9: Rd.Pin_1, J1.pin4
  N10: Rc.Pin_1, J1.pin3
  N11: Rb.Pin_1, J1.pin2
  N12: Ra.Pin_0, Qa.base
  N13: Ra.Pin_1, J1.pin1
  N14: Motor1.pin1, Motor1.pin2
  N15: R1.Pin_0, Q1.base
  N16: Motor2.pin1, Motor2.pin2
  N17: Motor3.pin1, Motor3.pin2
  N18: Q2.base, R2.Pin_0
  N19: Q3.base, R3.Pin_0

notes:
  Motor 1
  Power
  Arduino
  Motor 2
  Motor 3
